// Logisim project 串行进位的四位二进制并行加法器.circ as structural Verilog: 2 circuits, main circuit main
module main (
  input  A,
  input  B,
  input  C1,
  output S,
  output C0
);

  wire and_1_out, and_2_out, xor_1_out;

  xor xor_1 (xor_1_out, A, B);
  and and_1 (and_1_out, B, A);
  and and_2 (and_2_out, xor_1_out, C1);
  xor xor_2 (S, xor_1_out, C1);
  or or_1 (C0, and_2_out, and_1_out);
endmodule

module sd (
  input  C0,
  input  A3,
  input  B3,
  input  A2,
  input  B2,
  input  A1,
  input  B1,
  input  A0,
  input  B0,
  output S3,
  output S2,
  output S1,
  output S0,
  output C4
);

  wire main_2_c0, main_3_c0, main_4_c0;

  main main_1 (.A(A3), .B(B3), .C1(main_2_c0), .S(S3), .C0(C4));
  main main_2 (.A(A2), .B(B2), .C1(main_3_c0), .S(S2), .C0(main_2_c0));
  main main_3 (.A(A1), .B(B1), .C1(main_4_c0), .S(S1), .C0(main_3_c0));
  main main_4 (.A(A0), .B(B0), .C1(C0), .S(S0), .C0(main_4_c0));
endmodule
