// Logisim project 实验室门禁.circ as structural Verilog: 7 circuits, main circuit main
module main (
);

  wire button_1_out, button_2_out, button_3_out, \小型实验室门禁系统电路_1_out_4 , \小型实验室门禁系统电路_1_out_5 ,
       \小型实验室门禁系统电路_1_out_6 , \小型实验室门禁系统电路_1_out_7 , \小型实验室门禁系统电路_1_out_8 , \小型实验室门禁系统电路_1_out_9 ,
       \小型实验室门禁系统电路_1_out_10 , \小型实验室门禁系统电路_1_out_11 , \小型实验室门禁系统电路_1_out_12 , \小型实验室门禁系统电路_1_out_13 ,
       \小型实验室门禁系统电路_1_out_14 , \小型实验室门禁系统电路_1_out_15 , \小型实验室门禁系统电路_1_out_16 , \小型实验室门禁系统电路_1_out_17 ,
       \小型实验室门禁系统电路_1_报警 ;

  Button button_1 (.out(button_1_out));
  Button button_2 (.out(button_2_out));
  Button button_3 (.out(button_3_out));
  _7_Segment_Display u_7_segment_display_1 (
    .g(\小型实验室门禁系统电路_1_out_10 ), .f(\小型实验室门禁系统电路_1_out_9 ), .a(\小型实验室门禁系统电路_1_out_4 ),
    .b(\小型实验室门禁系统电路_1_out_5 ), .e(\小型实验室门禁系统电路_1_out_8 ), .d(\小型实验室门禁系统电路_1_out_7 ), .c(\小型实验室门禁系统电路_1_out_6 ));  // open: dp
  _7_Segment_Display u_7_segment_display_2 (
    .g(\小型实验室门禁系统电路_1_out_17 ), .f(\小型实验室门禁系统电路_1_out_16 ), .a(\小型实验室门禁系统电路_1_out_11 ),
    .b(\小型实验室门禁系统电路_1_out_12 ), .e(\小型实验室门禁系统电路_1_out_15 ), .d(\小型实验室门禁系统电路_1_out_14 ),
    .c(\小型实验室门禁系统电路_1_out_13 ));  // open: dp
  \小型实验室门禁系统电路  \u_小型实验室门禁系统电路_1  (
    .CPU(button_1_out), .CLR(button_2_out), .CPD(button_3_out), .out_4(\小型实验室门禁系统电路_1_out_4 ),
    .out_5(\小型实验室门禁系统电路_1_out_5 ), .out_6(\小型实验室门禁系统电路_1_out_6 ), .out_7(\小型实验室门禁系统电路_1_out_7 ),
    .out_8(\小型实验室门禁系统电路_1_out_8 ), .out_9(\小型实验室门禁系统电路_1_out_9 ), .out_10(\小型实验室门禁系统电路_1_out_10 ),
    .out_11(\小型实验室门禁系统电路_1_out_11 ), .out_12(\小型实验室门禁系统电路_1_out_12 ), .out_13(\小型实验室门禁系统电路_1_out_13 ),
    .out_14(\小型实验室门禁系统电路_1_out_14 ), .out_15(\小型实验室门禁系统电路_1_out_15 ), .out_16(\小型实验室门禁系统电路_1_out_16 ),
    .out_17(\小型实验室门禁系统电路_1_out_17 ), .\报警 (\小型实验室门禁系统电路_1_报警 ));
  LED led_1 (.in(\小型实验室门禁系统电路_1_报警 ));
endmodule

module _8421BCD (
  input  in_1,
  input  in_2,
  input  in_3,
  input  in_4,
  output S80,
  output S40,
  output S20,
  output S10,
  output S8,
  output S4,
  output S2,
  output S1
);

  wire and_1_out, or_1_out;

  or or_1 (or_1_out, in_3, in_2);
  and and_1 (and_1_out, in_1, or_1_out);
  \先行进位的四位二进制并行加法器_main  main_1 (
    .A0(in_4), .B0(1'b0), .C0(1'b0), .A1(in_3), .B1(and_1_out), .A2(in_2), .B2(and_1_out), .A3(in_1),
    .B3(1'b0), .S0(S1), .S1(S2), .S2(S4), .S3(S8), .Cout(S10));

  assign S20 = 1'b0;
  assign S40 = 1'b0;
  assign S80 = 1'b0;
endmodule

module \四位二进制可逆计数器  (
  input  CLR,
  input  CPU,
  input  CPD,
  output S0,
  output S1,
  output S2,
  output S3
);

  wire and_1_out, and_2_out, and_3_out, and_4_out, and_5_out, and_6_out, and_7_out, and_8_out, and_9_out,
       and_10_out, and_11_out, and_12_out, d_ff_1_qn, d_ff_2_qn, d_ff_3_qn, nand_1_out, nor_1_out, not_1_out,
       or_1_out, xor_1_out, xor_2_out, xor_3_out, xor_4_out, xor_5_out, xor_6_out, xor_7_out, xor_8_out;

  or or_1 (or_1_out, S1, S0, S2, S3);
  not not_1 (not_1_out, CLR);
  nand nand_1 (nand_1_out, S1, S0, S2, S3);
  and and_1 (and_1_out, nand_1_out, CPU);
  and and_2 (and_2_out, or_1_out, CPD);
  and and_3 (and_3_out, S0, and_1_out);
  xor xor_1 (xor_1_out, S1, and_3_out);
  and and_4 (and_4_out, S1, and_3_out);
  and and_5 (and_5_out, d_ff_1_qn, and_2_out);
  xor xor_2 (xor_2_out, and_4_out, S2);
  and and_6 (and_6_out, and_4_out, S2);
  xor xor_3 (xor_3_out, and_6_out, S3);
  and and_7 (and_7_out, d_ff_2_qn, and_5_out);
  xor xor_4 (xor_4_out, S0, and_1_out);
  xor xor_5 (xor_5_out, xor_2_out, and_7_out);
  and and_8 (and_8_out, d_ff_3_qn, and_7_out);
  xor xor_6 (xor_6_out, and_8_out, xor_3_out);
  nor nor_1 (nor_1_out, and_2_out, CLR, and_1_out);
  xor xor_7 (xor_7_out, xor_4_out, and_2_out);
  xor xor_8 (xor_8_out, xor_1_out, and_5_out);
  and and_9 (and_9_out, xor_7_out, not_1_out);
  and and_10 (and_10_out, xor_8_out, not_1_out);
  and and_11 (and_11_out, xor_5_out, not_1_out);
  and and_12 (and_12_out, xor_6_out, not_1_out);
  D_Flip_Flop d_ff_1 (.clk(nor_1_out), .D(and_9_out), .Q(S0), .Qn(d_ff_1_qn));  // open: preset, en, reset
  D_Flip_Flop d_ff_2 (.clk(nor_1_out), .D(and_10_out), .Q(S1), .Qn(d_ff_2_qn));  // open: preset, en, reset
  D_Flip_Flop d_ff_3 (.clk(nor_1_out), .D(and_11_out), .Q(S2), .Qn(d_ff_3_qn));  // open: preset, en, reset
  D_Flip_Flop d_ff_4 (.clk(nor_1_out), .D(and_12_out), .Q(S3));  // open: Qn, preset, en, reset
endmodule

module \段译码器  (
  input  A3,
  input  A2,
  input  A1,
  input  A0,
  output a,
  output b,
  output c,
  output d,
  output e,
  output f,
  output g
);

  wire and_1_out, and_2_out, and_3_out, and_4_out, and_5_out, and_6_out, and_7_out, and_8_out, and_9_out,
       and_10_out, and_11_out, and_12_out, and_13_out, and_14_out, and_15_out, and_16_out, and_17_out,
       and_18_out, and_19_out, and_20_out, and_21_out, not_1_out, not_2_out, not_3_out, not_4_out;

  not not_1 (not_1_out, A3);
  not not_2 (not_2_out, A2);
  not not_3 (not_3_out, A1);
  not not_4 (not_4_out, A0);
  and and_1 (and_1_out, not_2_out, not_3_out, not_4_out);
  and and_2 (and_2_out, not_1_out, not_2_out, A1);
  and and_3 (and_3_out, not_1_out, A2, A0);
  and and_4 (and_4_out, A3, not_3_out, A0);
  and and_5 (and_5_out, not_1_out, A1, A0);
  and and_6 (and_6_out, not_1_out, not_2_out);
  and and_7 (and_7_out, not_3_out, not_4_out);
  and and_8 (and_8_out, not_2_out, not_3_out);
  and and_9 (and_9_out, not_1_out, A2);
  and and_10 (and_10_out, not_2_out, A0);
  and and_11 (and_11_out, not_2_out, not_4_out);
  and and_12 (and_12_out, A2, not_3_out, A0);
  and and_13 (and_13_out, not_2_out, A1, A0);
  and and_14 (and_14_out, A2, A1, not_4_out);
  and and_15 (and_15_out, A1, not_4_out);
  and and_16 (and_16_out, not_3_out, not_4_out);
  and and_17 (and_17_out, A2, not_3_out);
  and and_18 (and_18_out, A2, not_4_out);
  and and_19 (and_19_out, A3, not_2_out, not_3_out);
  and and_20 (and_20_out, A3, not_2_out);
  and and_21 (and_21_out, not_2_out, A1);
  or or_1 (a, and_1_out, and_2_out, and_3_out, and_4_out);
  or or_2 (b, and_5_out, and_6_out, and_7_out, and_8_out);
  or or_3 (c, and_8_out, and_9_out, and_10_out);
  or or_4 (d, and_11_out, and_12_out, and_13_out, and_14_out);
  or or_5 (e, and_11_out, and_15_out);
  or or_6 (f, and_16_out, and_17_out, and_18_out, and_19_out);
  or or_7 (g, and_15_out, and_17_out, and_20_out, and_21_out);
endmodule

module \_7段数码显示管  (
  input  in_1,
  input  in_2,
  input  in_3,
  input  in_4
);

  wire n8421bcd_1_s1, n8421bcd_1_s2, n8421bcd_1_s4, n8421bcd_1_s8, n8421bcd_1_s10, n8421bcd_1_s20,
       n8421bcd_1_s40, n8421bcd_1_s80, \段译码器_1_a , \段译码器_1_b , \段译码器_1_c , \段译码器_1_d , \段译码器_1_e ,
       \段译码器_1_f , \段译码器_1_g , \段译码器_2_a , \段译码器_2_b , \段译码器_2_c , \段译码器_2_d , \段译码器_2_e , \段译码器_2_f ,
       \段译码器_2_g ;

  \段译码器  \u_段译码器_1  (
    .A3(n8421bcd_1_s80), .A2(n8421bcd_1_s40), .A1(n8421bcd_1_s20), .A0(n8421bcd_1_s10), .a(\段译码器_1_a ),
    .b(\段译码器_1_b ), .c(\段译码器_1_c ), .d(\段译码器_1_d ), .e(\段译码器_1_e ), .f(\段译码器_1_f ), .g(\段译码器_1_g ));
  _8421BCD u_8421bcd_1 (
    .S80(n8421bcd_1_s80), .S40(n8421bcd_1_s40), .S20(n8421bcd_1_s20), .S10(n8421bcd_1_s10),
    .S8(n8421bcd_1_s8), .S4(n8421bcd_1_s4), .S2(n8421bcd_1_s2), .S1(n8421bcd_1_s1), .in_1(in_1), .in_2(in_2),
    .in_3(in_3), .in_4(in_4));
  _7_Segment_Display u_7_segment_display_1 (
    .g(\段译码器_1_g ), .f(\段译码器_1_f ), .a(\段译码器_1_a ), .b(\段译码器_1_b ), .e(\段译码器_1_e ), .d(\段译码器_1_d ),
    .c(\段译码器_1_c ));  // open: dp
  \段译码器  \u_段译码器_2  (
    .A3(n8421bcd_1_s8), .A2(n8421bcd_1_s4), .A1(n8421bcd_1_s2), .A0(n8421bcd_1_s1), .a(\段译码器_2_a ),
    .b(\段译码器_2_b ), .c(\段译码器_2_c ), .d(\段译码器_2_d ), .e(\段译码器_2_e ), .f(\段译码器_2_f ), .g(\段译码器_2_g ));
  _7_Segment_Display u_7_segment_display_2 (
    .g(\段译码器_2_g ), .f(\段译码器_2_f ), .a(\段译码器_2_a ), .b(\段译码器_2_b ), .e(\段译码器_2_e ), .d(\段译码器_2_d ),
    .c(\段译码器_2_c ));  // open: dp
endmodule

module \报警系统  (
);

  wire and_1_out, button_1_out, button_2_out, button_3_out, n8421bcd_1_s1, n8421bcd_1_s2, n8421bcd_1_s4,
       n8421bcd_1_s8, n8421bcd_1_s10, n8421bcd_1_s20, n8421bcd_1_s40, n8421bcd_1_s80, \四位二进制可逆计数器_1_s0 ,
       \四位二进制可逆计数器_1_s1 , \四位二进制可逆计数器_1_s2 , \四位二进制可逆计数器_1_s3 , \段译码器_1_a , \段译码器_1_b , \段译码器_1_c ,
       \段译码器_1_d , \段译码器_1_e , \段译码器_1_f , \段译码器_1_g , \段译码器_2_a , \段译码器_2_b , \段译码器_2_c , \段译码器_2_d ,
       \段译码器_2_e , \段译码器_2_f , \段译码器_2_g ;

  Button button_1 (.out(button_1_out));
  Button button_2 (.out(button_2_out));
  Button button_3 (.out(button_3_out));
  \段译码器  \u_段译码器_1  (
    .A3(n8421bcd_1_s80), .A2(n8421bcd_1_s40), .A1(n8421bcd_1_s20), .A0(n8421bcd_1_s10), .a(\段译码器_1_a ),
    .b(\段译码器_1_b ), .c(\段译码器_1_c ), .d(\段译码器_1_d ), .e(\段译码器_1_e ), .f(\段译码器_1_f ), .g(\段译码器_1_g ));
  _7_Segment_Display u_7_segment_display_1 (
    .g(\段译码器_1_g ), .f(\段译码器_1_f ), .a(\段译码器_1_a ), .b(\段译码器_1_b ), .e(\段译码器_1_e ), .d(\段译码器_1_d ),
    .c(\段译码器_1_c ));  // open: dp
  _8421BCD u_8421bcd_1 (
    .S80(n8421bcd_1_s80), .S40(n8421bcd_1_s40), .S20(n8421bcd_1_s20), .S10(n8421bcd_1_s10),
    .S8(n8421bcd_1_s8), .S4(n8421bcd_1_s4), .S2(n8421bcd_1_s2), .S1(n8421bcd_1_s1), .in_1(\四位二进制可逆计数器_1_s3 ),
    .in_2(\四位二进制可逆计数器_1_s2 ), .in_3(\四位二进制可逆计数器_1_s1 ), .in_4(\四位二进制可逆计数器_1_s0 ));
  \四位二进制可逆计数器  \u_四位二进制可逆计数器_1  (
    .CLR(button_2_out), .CPU(button_1_out), .CPD(button_3_out), .S0(\四位二进制可逆计数器_1_s0 ),
    .S1(\四位二进制可逆计数器_1_s1 ), .S2(\四位二进制可逆计数器_1_s2 ), .S3(\四位二进制可逆计数器_1_s3 ));
  \段译码器  \u_段译码器_2  (
    .A3(n8421bcd_1_s8), .A2(n8421bcd_1_s4), .A1(n8421bcd_1_s2), .A0(n8421bcd_1_s1), .a(\段译码器_2_a ),
    .b(\段译码器_2_b ), .c(\段译码器_2_c ), .d(\段译码器_2_d ), .e(\段译码器_2_e ), .f(\段译码器_2_f ), .g(\段译码器_2_g ));
  and and_1 (and_1_out, \四位二进制可逆计数器_1_s3 , \四位二进制可逆计数器_1_s2 , \四位二进制可逆计数器_1_s1 , \四位二进制可逆计数器_1_s0 );
  _7_Segment_Display u_7_segment_display_2 (
    .g(\段译码器_2_g ), .f(\段译码器_2_f ), .a(\段译码器_2_a ), .b(\段译码器_2_b ), .e(\段译码器_2_e ), .d(\段译码器_2_d ),
    .c(\段译码器_2_c ));  // open: dp
  LED led_1 (.in(and_1_out));

  // Notes on the sheet:
  //   报警系统
endmodule

module \小型实验室门禁系统电路  (
  input  CPU,
  input  CLR,
  input  CPD,
  output out_4,
  output out_5,
  output out_6,
  output out_7,
  output out_8,
  output out_9,
  output out_10,
  output out_11,
  output out_12,
  output out_13,
  output out_14,
  output out_15,
  output out_16,
  output out_17,
  output \报警 
);

  wire n8421bcd_1_s1, n8421bcd_1_s2, n8421bcd_1_s4, n8421bcd_1_s8, n8421bcd_1_s10, n8421bcd_1_s20,
       n8421bcd_1_s40, n8421bcd_1_s80, \四位二进制可逆计数器_1_s0 , \四位二进制可逆计数器_1_s1 , \四位二进制可逆计数器_1_s2 ,
       \四位二进制可逆计数器_1_s3 ;

  _8421BCD u_8421bcd_1 (
    .S80(n8421bcd_1_s80), .S40(n8421bcd_1_s40), .S20(n8421bcd_1_s20), .S10(n8421bcd_1_s10),
    .S8(n8421bcd_1_s8), .S4(n8421bcd_1_s4), .S2(n8421bcd_1_s2), .S1(n8421bcd_1_s1), .in_1(\四位二进制可逆计数器_1_s3 ),
    .in_2(\四位二进制可逆计数器_1_s2 ), .in_3(\四位二进制可逆计数器_1_s1 ), .in_4(\四位二进制可逆计数器_1_s0 ));
  \四位二进制可逆计数器  \u_四位二进制可逆计数器_1  (
    .CLR(CLR), .CPU(CPU), .CPD(CPD), .S0(\四位二进制可逆计数器_1_s0 ), .S1(\四位二进制可逆计数器_1_s1 ), .S2(\四位二进制可逆计数器_1_s2 ),
    .S3(\四位二进制可逆计数器_1_s3 ));
  \段译码器  \u_段译码器_1  (
    .A3(n8421bcd_1_s80), .A2(n8421bcd_1_s40), .A1(n8421bcd_1_s20), .A0(n8421bcd_1_s10), .a(out_4), .b(out_5),
    .c(out_6), .d(out_7), .e(out_8), .f(out_9), .g(out_10));
  \段译码器  \u_段译码器_2  (
    .A3(n8421bcd_1_s8), .A2(n8421bcd_1_s4), .A1(n8421bcd_1_s2), .A0(n8421bcd_1_s1), .a(out_11), .b(out_12),
    .c(out_13), .d(out_14), .e(out_15), .f(out_16), .g(out_17));
  and and_1 (\报警 , \四位二进制可逆计数器_1_s3 , \四位二进制可逆计数器_1_s2 , \四位二进制可逆计数器_1_s1 , \四位二进制可逆计数器_1_s0 );
endmodule
