// Logisim project 除法器.circ as structural Verilog
module \四位除法器  (
  input  [3:0] N2,
  input  [3:0] D,
  output [3:0] quot,
  output [3:0] rem
);

  wire comparator_1_eq, comparator_1_gt, comparator_2_eq, comparator_2_gt, comparator_3_eq, comparator_3_gt,
       comparator_4_eq, comparator_4_gt, or_1_out, or_2_out, or_3_out, or_4_out;
  wire [3:0] multiplexer_1_out, multiplexer_2_out, multiplexer_3_out, multiplexer_4_out, subtractor_1_out,
       subtractor_2_out, subtractor_3_out, subtractor_4_out;
  wire [7:0] bit_extender_1_out, shifter_1_out, shifter_2_out, shifter_3_out, shifter_4_out, X;

  assign bit_extender_1_out = {{4{1'b0}}, N2};  // Bit_Extender bit_extender_1
  Shifter shifter_1 (.in(bit_extender_1_out), .\dist (3'b001), .out(shifter_1_out));
  Shifter shifter_2 (.in(X), .\dist (3'b001), .out(shifter_2_out));
  Subtractor #(.width(4)) subtractor_1 (.a(shifter_1_out[7:4]), .b(D), .out(subtractor_1_out));  // open: bin, bout
  Comparator #(.width(4), .mode("unsigned")) comparator_1 (
    .a(shifter_1_out[7:4]), .b(D), .gt(comparator_1_gt), .eq(comparator_1_eq));  // open: lt
  Subtractor #(.width(4)) subtractor_2 (.a(shifter_2_out[7:4]), .b(D), .out(subtractor_2_out));  // open: bin, bout
  Comparator #(.width(4), .mode("unsigned")) comparator_2 (
    .a(shifter_2_out[7:4]), .b(D), .gt(comparator_2_gt), .eq(comparator_2_eq));  // open: lt
  Multiplexer #(.width(4), .enable("false")) multiplexer_1 (
    .in0(shifter_1_out[3:0]), .in1({shifter_1_out[3:1], 1'b1}), .out(multiplexer_1_out), .sel(or_1_out));
  or or_1 (or_1_out, comparator_1_gt, comparator_1_eq);
  Multiplexer #(.width(4), .enable("false")) multiplexer_2 (
    .in0(shifter_2_out[3:0]), .in1({shifter_2_out[3:1], 1'b1}), .out(multiplexer_2_out), .sel(or_2_out));
  or or_2 (or_2_out, comparator_2_gt, comparator_2_eq);
  Multiplexer #(.width(4), .enable("false")) multiplexer_3 (
    .in0(shifter_1_out[7:4]), .in1(subtractor_1_out), .out(multiplexer_3_out), .sel(or_1_out));
  Multiplexer #(.width(4), .enable("false")) multiplexer_4 (
    .in0(shifter_2_out[7:4]), .in1(subtractor_2_out), .out(multiplexer_4_out), .sel(or_2_out));
  Shifter shifter_3 (.in({multiplexer_3_out, multiplexer_1_out}), .\dist (3'b001), .out(shifter_3_out));
  Shifter shifter_4 (.in({multiplexer_4_out, multiplexer_2_out}), .\dist (3'b001), .out(shifter_4_out));
  Subtractor #(.width(4)) subtractor_3 (.a(shifter_3_out[7:4]), .b(D), .out(subtractor_3_out));  // open: bin, bout
  Comparator #(.width(4), .mode("unsigned")) comparator_3 (
    .a(shifter_3_out[7:4]), .b(D), .gt(comparator_3_gt), .eq(comparator_3_eq));  // open: lt
  Subtractor #(.width(4)) subtractor_4 (.a(shifter_4_out[7:4]), .b(D), .out(subtractor_4_out));  // open: bin, bout
  Comparator #(.width(4), .mode("unsigned")) comparator_4 (
    .a(shifter_4_out[7:4]), .b(D), .gt(comparator_4_gt), .eq(comparator_4_eq));  // open: lt
  Multiplexer #(.width(4), .enable("false")) multiplexer_5 (
    .in0(shifter_3_out[3:0]), .in1({shifter_3_out[3:1], 1'b1}), .out(X[3:0]), .sel(or_3_out));
  Multiplexer #(.width(4), .enable("false")) multiplexer_6 (
    .in0(shifter_3_out[7:4]), .in1(subtractor_3_out), .out(X[7:4]), .sel(or_3_out));
  or or_3 (or_3_out, comparator_3_gt, comparator_3_eq);
  Multiplexer #(.width(4), .enable("false")) multiplexer_7 (
    .in0(shifter_4_out[3:0]), .in1({shifter_4_out[3:1], 1'b1}), .out(quot), .sel(or_4_out));
  Multiplexer #(.width(4), .enable("false")) multiplexer_8 (
    .in0(shifter_4_out[7:4]), .in1(subtractor_4_out), .out(rem), .sel(or_4_out));
  or or_4 (or_4_out, comparator_4_gt, comparator_4_eq);
endmodule

module \_32位除法器  (
  input  [31:0] N1,
  input  [31:0] N2,
  input  [31:0] D,
  output [31:0] QUOT,
  output [31:0] REM
);

  wire comparator_1_eq, comparator_1_gt, or_1_out;
  wire [31:0] subtractor_1_out;

  Subtractor #(.width(32)) subtractor_1 (.a({N1[30:0], N2[31]}), .b(D), .out(subtractor_1_out));  // open: bin, bout
  Comparator #(.width(32), .mode("unsigned")) comparator_1 (
    .a({N1[30:0], N2[31]}), .b(D), .gt(comparator_1_gt), .eq(comparator_1_eq));  // open: lt
  or or_1 (or_1_out, comparator_1_gt, comparator_1_eq);
  Multiplexer #(.width(32), .enable("false")) multiplexer_1 (
    .in0({N2[30:0], 1'b1}), .in1({N2[30:0], 1'b0}), .out(QUOT), .sel(or_1_out));
  Multiplexer #(.width(32), .enable("false")) multiplexer_2 (
    .in0({N1[30:0], N2[31]}), .in1(subtractor_1_out), .out(REM), .sel(or_1_out));
endmodule

module \三十二除法器  (
  output [31:0] out_1,
  output [31:0] out_2
);

  wire [31:0] \n32位除法器_1_quot , \n32位除法器_1_rem , \n32位除法器_2_quot , \n32位除法器_2_rem , \n32位除法器_3_quot ,
       \n32位除法器_3_rem , \n32位除法器_4_quot , \n32位除法器_4_rem , \n32位除法器_5_quot , \n32位除法器_5_rem ,
       \n32位除法器_6_quot , \n32位除法器_6_rem , \n32位除法器_7_quot , \n32位除法器_7_rem , \n32位除法器_8_quot ,
       \n32位除法器_8_rem , \n32位除法器_9_quot , \n32位除法器_9_rem , \n32位除法器_10_quot , \n32位除法器_10_rem ,
       \n32位除法器_11_quot , \n32位除法器_11_rem , \n32位除法器_12_quot , \n32位除法器_12_rem , \n32位除法器_13_quot ,
       \n32位除法器_13_rem , \n32位除法器_14_quot , \n32位除法器_14_rem , \n32位除法器_15_quot , \n32位除法器_15_rem ,
       \n32位除法器_16_quot , \n32位除法器_16_rem , \n32位除法器_17_quot , \n32位除法器_17_rem , \n32位除法器_18_quot ,
       \n32位除法器_18_rem , \n32位除法器_19_quot , \n32位除法器_19_rem , \n32位除法器_20_quot , \n32位除法器_20_rem ,
       \n32位除法器_21_quot , \n32位除法器_21_rem , \n32位除法器_22_quot , \n32位除法器_22_rem , \n32位除法器_23_quot ,
       \n32位除法器_23_rem , \n32位除法器_24_quot , \n32位除法器_24_rem , Q1, Q2, Q3, Q4, Q5, Q6, Q7, R1, R2, R3, R4, R5,
       R6, R7;

  \_32位除法器  \u_32位除法器_1  (.N1({32{1'b0}}), .N2(32'he), .D(32'h9), .QUOT(\n32位除法器_1_quot ), .REM(\n32位除法器_1_rem ));
  \_32位除法器  \u_32位除法器_2  (.N1(R1), .N2(Q1), .D(32'h9), .QUOT(\n32位除法器_2_quot ), .REM(\n32位除法器_2_rem ));
  \_32位除法器  \u_32位除法器_3  (.N1(R2), .N2(Q2), .D(32'h9), .QUOT(\n32位除法器_3_quot ), .REM(\n32位除法器_3_rem ));
  \_32位除法器  \u_32位除法器_4  (.N1(R3), .N2(Q3), .D(32'h9), .QUOT(\n32位除法器_4_quot ), .REM(\n32位除法器_4_rem ));
  \_32位除法器  \u_32位除法器_5  (.N1(R4), .N2(Q4), .D(32'h9), .QUOT(\n32位除法器_5_quot ), .REM(\n32位除法器_5_rem ));
  \_32位除法器  \u_32位除法器_6  (.N1(R5), .N2(Q5), .D(32'h9), .QUOT(\n32位除法器_6_quot ), .REM(\n32位除法器_6_rem ));
  \_32位除法器  \u_32位除法器_7  (.N1(R6), .N2(Q6), .D(32'h9), .QUOT(\n32位除法器_7_quot ), .REM(\n32位除法器_7_rem ));
  \_32位除法器  \u_32位除法器_8  (.N1(R7), .N2(Q7), .D(32'h9), .QUOT(\n32位除法器_8_quot ), .REM(\n32位除法器_8_rem ));
  \_32位除法器  \u_32位除法器_9  (
    .N1(\n32位除法器_1_rem ), .N2(\n32位除法器_1_quot ), .D(32'h9), .QUOT(\n32位除法器_9_quot ), .REM(\n32位除法器_9_rem ));
  \_32位除法器  \u_32位除法器_10  (
    .N1(\n32位除法器_2_rem ), .N2(\n32位除法器_2_quot ), .D(32'h9), .QUOT(\n32位除法器_10_quot ), .REM(\n32位除法器_10_rem ));
  \_32位除法器  \u_32位除法器_11  (
    .N1(\n32位除法器_3_rem ), .N2(\n32位除法器_3_quot ), .D(32'h9), .QUOT(\n32位除法器_11_quot ), .REM(\n32位除法器_11_rem ));
  \_32位除法器  \u_32位除法器_12  (
    .N1(\n32位除法器_4_rem ), .N2(\n32位除法器_4_quot ), .D(32'h9), .QUOT(\n32位除法器_12_quot ), .REM(\n32位除法器_12_rem ));
  \_32位除法器  \u_32位除法器_13  (
    .N1(\n32位除法器_5_rem ), .N2(\n32位除法器_5_quot ), .D(32'h9), .QUOT(\n32位除法器_13_quot ), .REM(\n32位除法器_13_rem ));
  \_32位除法器  \u_32位除法器_14  (
    .N1(\n32位除法器_6_rem ), .N2(\n32位除法器_6_quot ), .D(32'h9), .QUOT(\n32位除法器_14_quot ), .REM(\n32位除法器_14_rem ));
  \_32位除法器  \u_32位除法器_15  (
    .N1(\n32位除法器_7_rem ), .N2(\n32位除法器_7_quot ), .D(32'h9), .QUOT(\n32位除法器_15_quot ), .REM(\n32位除法器_15_rem ));
  \_32位除法器  \u_32位除法器_16  (
    .N1(\n32位除法器_8_rem ), .N2(\n32位除法器_8_quot ), .D(32'h9), .QUOT(\n32位除法器_16_quot ), .REM(\n32位除法器_16_rem ));
  \_32位除法器  \u_32位除法器_17  (
    .N1(\n32位除法器_9_rem ), .N2(\n32位除法器_9_quot ), .D(32'h9), .QUOT(\n32位除法器_17_quot ), .REM(\n32位除法器_17_rem ));
  \_32位除法器  \u_32位除法器_18  (
    .N1(\n32位除法器_10_rem ), .N2(\n32位除法器_10_quot ), .D(32'h9), .QUOT(\n32位除法器_18_quot ), .REM(\n32位除法器_18_rem ));
  \_32位除法器  \u_32位除法器_19  (
    .N1(\n32位除法器_11_rem ), .N2(\n32位除法器_11_quot ), .D(32'h9), .QUOT(\n32位除法器_19_quot ), .REM(\n32位除法器_19_rem ));
  \_32位除法器  \u_32位除法器_20  (
    .N1(\n32位除法器_12_rem ), .N2(\n32位除法器_12_quot ), .D(32'h9), .QUOT(\n32位除法器_20_quot ), .REM(\n32位除法器_20_rem ));
  \_32位除法器  \u_32位除法器_21  (
    .N1(\n32位除法器_13_rem ), .N2(\n32位除法器_13_quot ), .D(32'h9), .QUOT(\n32位除法器_21_quot ), .REM(\n32位除法器_21_rem ));
  \_32位除法器  \u_32位除法器_22  (
    .N1(\n32位除法器_14_rem ), .N2(\n32位除法器_14_quot ), .D(32'h9), .QUOT(\n32位除法器_22_quot ), .REM(\n32位除法器_22_rem ));
  \_32位除法器  \u_32位除法器_23  (
    .N1(\n32位除法器_15_rem ), .N2(\n32位除法器_15_quot ), .D(32'h9), .QUOT(\n32位除法器_23_quot ), .REM(\n32位除法器_23_rem ));
  \_32位除法器  \u_32位除法器_24  (
    .N1(\n32位除法器_16_rem ), .N2(\n32位除法器_16_quot ), .D(32'h9), .QUOT(\n32位除法器_24_quot ), .REM(\n32位除法器_24_rem ));
  \_32位除法器  \u_32位除法器_25  (.N1(\n32位除法器_17_rem ), .N2(\n32位除法器_17_quot ), .D(32'h9), .QUOT(Q1), .REM(R1));
  \_32位除法器  \u_32位除法器_26  (.N1(\n32位除法器_18_rem ), .N2(\n32位除法器_18_quot ), .D(32'h9), .QUOT(Q2), .REM(R2));
  \_32位除法器  \u_32位除法器_27  (.N1(\n32位除法器_19_rem ), .N2(\n32位除法器_19_quot ), .D(32'h9), .QUOT(Q3), .REM(R3));
  \_32位除法器  \u_32位除法器_28  (.N1(\n32位除法器_20_rem ), .N2(\n32位除法器_20_quot ), .D(32'h9), .QUOT(Q4), .REM(R4));
  \_32位除法器  \u_32位除法器_29  (.N1(\n32位除法器_21_rem ), .N2(\n32位除法器_21_quot ), .D(32'h9), .QUOT(Q5), .REM(R5));
  \_32位除法器  \u_32位除法器_30  (.N1(\n32位除法器_22_rem ), .N2(\n32位除法器_22_quot ), .D(32'h9), .QUOT(Q6), .REM(R6));
  \_32位除法器  \u_32位除法器_31  (.N1(\n32位除法器_23_rem ), .N2(\n32位除法器_23_quot ), .D(32'h9), .QUOT(Q7), .REM(R7));
  \_32位除法器  \u_32位除法器_32  (.N1(\n32位除法器_24_rem ), .N2(\n32位除法器_24_quot ), .D(32'h9), .QUOT(out_1), .REM(out_2));
endmodule
