// Logisim project 第3次实验.circ as structural Verilog
module \可逆计数器  (
  input  CPU,
  input  in_2,
  input  in_3,
  input  CPD,
  input  in_5,
  input  in_6,
  input  in_7,
  input  CLR,
  output Q3,
  output Q2,
  output Q1,
  output Q0
);

  wire and_1_out, and_2_out, and_3_out, and_4_out, and_5_out, and_6_out, and_7_out, and_8_out, and_9_out,
       and_10_out, and_11_out, and_12_out, and_13_out, and_14_out, d_ff_1_qn, d_ff_2_qn, d_ff_3_qn,
       d_ff_4_qn, not_1_out, not_2_out, not_3_out, not_4_out, not_5_out, not_6_out, not_7_out, not_8_out,
       or_1_out, or_2_out, or_3_out, or_4_out, or_5_out, or_6_out, or_7_out, or_8_out;

  and and_1 (and_1_out, CPU, Q0, Q1, Q2);
  and and_2 (and_2_out, d_ff_2_qn, d_ff_4_qn, d_ff_3_qn, CPD);
  and and_3 (and_3_out, CPU, Q1, Q0);
  and and_4 (and_4_out, CPD, d_ff_4_qn, d_ff_3_qn);
  and and_5 (and_5_out, CPU, Q0);
  and and_6 (and_6_out, CPD, d_ff_4_qn);
  or or_1 (or_1_out, and_1_out, and_2_out);
  or or_2 (or_2_out, and_3_out, and_4_out);
  or or_3 (or_3_out, and_5_out, and_6_out);
  not not_1 (not_1_out, or_1_out);
  not not_2 (not_2_out, or_2_out);
  not not_3 (not_3_out, or_3_out);
  or or_4 (or_4_out, CPD, CPU);
  not not_4 (not_4_out, or_4_out);
  or or_5 (or_5_out, CLR, and_9_out);
  or or_6 (or_6_out, CLR, and_11_out);
  or or_7 (or_7_out, CLR, and_13_out);
  D_Flip_Flop d_ff_1 (
    .clk(not_1_out), .D(d_ff_1_qn), .Q(Q3), .Qn(d_ff_1_qn), .preset(and_8_out), .reset(or_8_out));  // open: en
  or or_8 (or_8_out, CLR, and_7_out);
  and and_7 (and_7_out, in_2, not_5_out);
  and and_8 (and_8_out, in_2, in_3);
  D_Flip_Flop d_ff_2 (
    .clk(not_2_out), .D(d_ff_2_qn), .Q(Q2), .Qn(d_ff_2_qn), .preset(and_10_out), .reset(or_5_out));  // open: en
  and and_9 (and_9_out, in_2, not_6_out);
  and and_10 (and_10_out, in_2, in_5);
  D_Flip_Flop d_ff_3 (
    .clk(not_3_out), .D(d_ff_3_qn), .Q(Q1), .Qn(d_ff_3_qn), .preset(and_12_out), .reset(or_6_out));  // open: en
  and and_11 (and_11_out, in_2, not_7_out);
  and and_12 (and_12_out, in_2, in_6);
  D_Flip_Flop d_ff_4 (
    .clk(not_4_out), .D(d_ff_4_qn), .Q(Q0), .Qn(d_ff_4_qn), .preset(and_14_out), .reset(or_7_out));  // open: en
  and and_13 (and_13_out, in_2, not_8_out);
  and and_14 (and_14_out, in_2, in_7);
  not not_5 (not_5_out, in_3);
  not not_6 (not_6_out, in_5);
  not not_7 (not_7_out, in_6);
  not not_8 (not_8_out, in_7);
endmodule

module \_60进制计数器  (
  input  CPu,
  input  Adj,
  input  CPd,
  input  Clr,
  output out_5,
  output out_6,
  output out_7,
  output out_8,
  output out_9,
  output out_10,
  output out_11,
  output out_12,
  output out_13
);

  wire and_1_out, and_2_out, and_3_out, and_4_out, and_5_out, not_1_out, not_2_out, not_3_out, or_1_out,
       or_2_out, or_3_out;

  or or_1 (or_1_out, out_5, out_6, out_7, out_8, out_9, out_10, out_11, out_12);
  and and_1 (and_1_out, Adj, or_1_out, CPd);
  or or_2 (or_2_out, Clr, and_2_out);
  or or_3 (or_3_out, Clr, and_5_out);
  \可逆计数器  \u_可逆计数器_1  (
    .CPU(CPu), .CPD(and_1_out), .Q3(out_9), .Q2(out_10), .Q1(out_11), .Q0(out_12), .CLR(or_2_out),
    .in_2(and_4_out), .in_3(1'b1), .in_5(1'b0), .in_6(1'b0), .in_7(1'b1));
  \可逆计数器  \u_可逆计数器_2  (
    .CPU(and_2_out), .CPD(and_4_out), .Q3(out_5), .Q2(out_6), .Q1(out_7), .Q0(out_8), .CLR(or_3_out),
    .in_2(and_3_out), .in_3(1'b0), .in_5(1'b0), .in_6(1'b0), .in_7(1'b0));
  not not_1 (not_1_out, out_10);
  not not_2 (not_2_out, out_12);
  and and_2 (and_2_out, out_9, out_11, not_2_out);
  and and_3 (and_3_out, out_5, out_6, out_7, out_8);
  and and_4 (and_4_out, out_12, out_11, out_10, out_9);
  not not_3 (not_3_out, out_5);
  and and_5 (and_5_out, not_3_out, out_6, out_7);
  not not_4 (out_13, and_5_out);
endmodule

module \_12或24进制计数器  (
  input  Set,
  input  in_2,
  input  in_3,
  input  in_4,
  input  in_5,
  output out_6,
  output out_7,
  output out_8,
  output out_9,
  output out_10,
  output out_11,
  output out_12,
  output out_13,
  output out_14
);

  wire and_1_out, and_2_out, not_1_out, not_2_out, not_3_out, or_1_out, or_2_out, or_3_out;

  not not_1 (not_1_out, Set);
  or or_1 (or_1_out, in_5, or_2_out);
  \_60进制计数器  \u_60进制计数器_1  (
    .CPu(in_2), .CPd(in_4), .Clr(or_1_out), .out_5(out_6), .out_6(out_7), .out_7(out_8), .out_8(out_9),
    .out_9(out_10), .out_10(out_11), .out_11(out_12), .out_12(out_13), .Adj(in_3));  // open: out_13
  or or_2 (or_2_out, and_2_out, and_1_out);
  not not_2 (not_2_out, out_13);
  not not_3 (not_3_out, out_13);
  and and_1 (and_1_out, not_2_out, out_11, Set, out_8);
  and and_2 (and_2_out, out_9, not_1_out, out_12, not_3_out);
  not not_4 (out_14, or_3_out);
  or or_3 (or_3_out, and_1_out, and_2_out);
endmodule

module \显示上午下午电路  (
  input  TT,
  input  A_F,
  output [4:0] out_3,
  output [4:0] out_4,
  output [4:0] out_5,
  output [4:0] out_6
);

  wire not_1_out, not_2_out;
  wire [4:0] and_1_out, and_2_out, and_3_out, and_4_out, bit_extender_1_out, bit_extender_2_out,
       bit_extender_3_out, bit_extender_4_out, bit_extender_5_out, or_1_out, or_2_out;

  assign bit_extender_1_out = {{4{TT}}, TT};  // Bit_Extender bit_extender_1
  not not_1 (not_1_out, A_F);
  not not_2 (not_2_out, A_F);
  assign and_1_out = 5'b00001 & bit_extender_2_out;  // AND_Gate and_1, 5 bits wide
  assign bit_extender_2_out = {{4{not_1_out}}, not_1_out};  // Bit_Extender bit_extender_2
  assign and_2_out = 5'b10000 & bit_extender_3_out;  // AND_Gate and_2, 5 bits wide
  assign bit_extender_3_out = {{4{A_F}}, A_F};  // Bit_Extender bit_extender_3
  assign and_3_out = 5'b00101 & bit_extender_4_out;  // AND_Gate and_3, 5 bits wide
  assign bit_extender_4_out = {{4{not_2_out}}, not_2_out};  // Bit_Extender bit_extender_4
  assign and_4_out = 5'b10100 & bit_extender_5_out;  // AND_Gate and_4, 5 bits wide
  assign bit_extender_5_out = {{4{A_F}}, A_F};  // Bit_Extender bit_extender_5
  assign out_4 = bit_extender_1_out & or_2_out;  // AND_Gate and_5, 5 bits wide
  assign out_5 = bit_extender_1_out & {5{1'b1}};  // AND_Gate and_6, 5 bits wide
  assign out_3 = bit_extender_1_out & or_1_out;  // AND_Gate and_7, 5 bits wide
  assign or_1_out = and_1_out | and_2_out;  // OR_Gate or_1, 5 bits wide
  assign or_2_out = and_3_out | and_4_out;  // OR_Gate or_2, 5 bits wide

  assign out_6 = out_3;
endmodule

module \整点报时电路  (
  input  in_1,
  input  in_2,
  output out_3
);

  wire and_2_out, and_3_out, \n8hz转1hz_1_out_2 , \n60进制计数器_1_out_8 , \n60进制计数器_1_out_9 , \n60进制计数器_1_out_10 ,
       \n60进制计数器_1_out_11 , \n60进制计数器_1_out_12 , or_1_out, or_2_out;

  and and_1 (out_3, \n8hz转1hz_1_out_2 , or_2_out);
  or or_1 (or_1_out, in_1, or_2_out);
  \_8Hz转1Hz  \u_8hz转1hz_1  (.out_2(\n8hz转1hz_1_out_2 ));  // open: in_1
  \_60进制计数器  \u_60进制计数器_1  (
    .CPu(and_2_out), .CPd(1'b0), .Clr(and_3_out), .out_8(\n60进制计数器_1_out_8 ), .out_9(\n60进制计数器_1_out_9 ),
    .out_10(\n60进制计数器_1_out_10 ), .out_11(\n60进制计数器_1_out_11 ), .out_12(\n60进制计数器_1_out_12 ), .Adj(1'b0));  // open: out_13, out_5, out_6, out_7
  and and_2 (and_2_out, or_1_out, \n8hz转1hz_1_out_2 );
  or or_2 (or_2_out, \n60进制计数器_1_out_9 , \n60进制计数器_1_out_10 , \n60进制计数器_1_out_11 , \n60进制计数器_1_out_12 );
  and and_3 (and_3_out, and_2_out, \n60进制计数器_1_out_8 );
endmodule

module \_8Hz转1Hz  (
  input  in_1,
  output out_2
);

  wire d_ff_1_qn, \可逆计数器_1_q1 ;

  \可逆计数器  \u_可逆计数器_1  (
    .CPU(in_1), .CPD(1'b0), .Q1(\可逆计数器_1_q1 ), .CLR(\可逆计数器_1_q1 ));  // open: Q3, Q2, Q0, in_2, in_3, in_5, in_6, in_7
  D_Flip_Flop d_ff_1 (.clk(\可逆计数器_1_q1 ), .D(d_ff_1_qn), .Q(out_2), .Qn(d_ff_1_qn));  // open: preset, en, reset
endmodule

module \_60进制计数器封装  (
  input  in_1,
  input  in_2,
  output out_3
);

  wire button_1_out, button_2_out;
  wire [3:0] \n60进制计数器_1_out_8 , \n60进制计数器_1_out_12 ;

  Button button_1 (.out(button_1_out));
  Button button_2 (.out(button_2_out));
  Hex_Digit_Display hex_digit_display_1 (.value(\n60进制计数器_1_out_8 ));  // open: dp
  Hex_Digit_Display hex_digit_display_2 (.value(\n60进制计数器_1_out_12 ));  // open: dp
  \_60进制计数器  \u_60进制计数器_1  (
    .CPu(button_1_out), .CPd(button_2_out), .Clr(in_2), .out_13(out_3), .out_5(\n60进制计数器_1_out_8 [3]),
    .out_6(\n60进制计数器_1_out_8 [2]), .out_7(\n60进制计数器_1_out_8 [1]), .out_8(\n60进制计数器_1_out_8 [0]),
    .out_9(\n60进制计数器_1_out_12 [3]), .out_10(\n60进制计数器_1_out_12 [2]), .out_11(\n60进制计数器_1_out_12 [1]),
    .out_12(\n60进制计数器_1_out_12 [0]), .Adj(in_1));
endmodule

module \_12或24进制计数器封装  (
  input  in_1,
  input  in_2,
  input  in_3,
  output out_4
);

  wire button_1_out, button_2_out;
  wire [3:0] \n12或24进制计数器_1_out_9 , \n12或24进制计数器_1_out_13 ;

  Button button_1 (.out(button_1_out));
  Button button_2 (.out(button_2_out));
  Hex_Digit_Display hex_digit_display_1 (.value(\n12或24进制计数器_1_out_9 ));  // open: dp
  Hex_Digit_Display hex_digit_display_2 (.value(\n12或24进制计数器_1_out_13 ));  // open: dp
  \_12或24进制计数器  \u_12或24进制计数器_1  (
    .Set(in_2), .in_2(button_1_out), .in_3(in_1), .in_4(button_2_out), .out_14(out_4), .in_5(in_3),
    .out_6(\n12或24进制计数器_1_out_9 [3]), .out_7(\n12或24进制计数器_1_out_9 [2]), .out_8(\n12或24进制计数器_1_out_9 [1]),
    .out_9(\n12或24进制计数器_1_out_9 [0]), .out_10(\n12或24进制计数器_1_out_13 [3]), .out_11(\n12或24进制计数器_1_out_13 [2]),
    .out_12(\n12或24进制计数器_1_out_13 [1]), .out_13(\n12或24进制计数器_1_out_13 [0]));
endmodule

module \显示上下午封装  (
  input  in_1,
  input  in_2
);

  wire [4:0] \显示上午下午电路_1_out_3 , \显示上午下午电路_1_out_4 , \显示上午下午电路_1_out_5 , \显示上午下午电路_1_out_6 ;

  DotMatrix #(.matrixcols(4), .matrixrows(5)) dotmatrix_1 (
    .col0(\显示上午下午电路_1_out_6 ), .col1(\显示上午下午电路_1_out_5 ), .col2(\显示上午下午电路_1_out_4 ), .col3(\显示上午下午电路_1_out_3 ));
  \显示上午下午电路  \u_显示上午下午电路_1  (
    .TT(in_2), .A_F(in_1), .out_6(\显示上午下午电路_1_out_6 ), .out_5(\显示上午下午电路_1_out_5 ),
    .out_4(\显示上午下午电路_1_out_4 ), .out_3(\显示上午下午电路_1_out_3 ));
endmodule

module \整点报时封装  (
  input  in_1
);

  wire clock_1_out, \整点报时电路_1_out_3 ;

  Clock clock_1 (.out(clock_1_out));
  \整点报时电路  \u_整点报时电路_1  (.in_1(in_1), .out_3(\整点报时电路_1_out_3 ), .in_2(clock_1_out));
  LED led_1 (.in(\整点报时电路_1_out_3 ));
endmodule

module \数字钟电路  (
  input  in_1,
  input  Adj1,
  input  Adj0,
  input  CPu,
  input  CPd,
  input  Clr,
  input  in_7,
  output [4:0] out_8,
  output [4:0] out_9,
  output [4:0] out_10,
  output [4:0] out_11,
  output [3:0] out_12,
  output [3:0] out_13,
  output [3:0] out_14,
  output [3:0] out_15,
  output [3:0] out_16,
  output [3:0] out_17,
  output out_18
);

  wire and_1_out, and_2_out, and_3_out, and_4_out, and_5_out, and_6_out, and_7_out, and_8_out, and_9_out,
       comparator_1_gt, \n8hz转1hz_1_out_2 , \n60进制计数器_1_out_13 , \n60进制计数器_2_out_13 , nor_1_out, not_1_out,
       not_2_out, not_3_out, not_4_out, or_1_out, or_2_out;
  wire [3:0] multiplexer_3_out, multiplexer_3_out_2, \n12或24进制计数器_1_out_9 , \n12或24进制计数器_1_out_13 ;
  wire [7:0] \bcd转2进制_1_out_3 , \n2进制转bcd_1_out_2 , subtractor_1_out;

  not not_1 (not_1_out, Adj1);
  \显示上午下午电路  \u_显示上午下午电路_1  (
    .TT(not_2_out), .A_F(comparator_1_gt), .out_6(out_8), .out_5(out_9), .out_4(out_10), .out_3(out_11));
  not not_2 (not_2_out, in_1);
  not not_3 (not_3_out, \n60进制计数器_1_out_13 );
  and and_1 (and_1_out, CPu, and_2_out);
  and and_2 (and_2_out, not_1_out, Adj0);
  and and_3 (and_3_out, and_2_out, CPd);
  and and_4 (and_4_out, Adj1, Adj0);
  or or_1 (or_1_out, not_3_out, and_1_out);
  and and_5 (and_5_out, CPu, and_4_out);
  and and_6 (and_6_out, and_4_out, CPd);
  \BCD转2进制  \bcd转2进制_1  (.in_1(\n12或24进制计数器_1_out_13 ), .in_2(\n12或24进制计数器_1_out_9 ), .out_3(\bcd转2进制_1_out_3 ));
  Subtractor subtractor_1 (.a(\bcd转2进制_1_out_3 ), .b(8'hc), .out(subtractor_1_out));  // open: bin, bout
  Multiplexer #(.width(4)) multiplexer_1 (
    .in0(multiplexer_3_out), .in1(\n12或24进制计数器_1_out_13 ), .out(out_13), .sel(in_1));  // open: en
  Multiplexer #(.width(4)) multiplexer_2 (
    .in0(multiplexer_3_out_2), .in1(\n12或24进制计数器_1_out_9 ), .out(out_12), .sel(in_1));  // open: en
  \_8Hz转1Hz  \u_8hz转1hz_1  (.in_1(in_7), .out_2(\n8hz转1hz_1_out_2 ));
  \_2进制转BCD  \u_2进制转bcd_1  (.in_1(subtractor_1_out), .out_2(\n2进制转bcd_1_out_2 ));
  \_12或24进制计数器  \u_12或24进制计数器_1  (
    .Set(1'b1), .in_2(or_1_out), .in_3(and_2_out), .in_4(and_3_out), .in_5(Clr),
    .out_6(\n12或24进制计数器_1_out_9 [3]), .out_7(\n12或24进制计数器_1_out_9 [2]), .out_8(\n12或24进制计数器_1_out_9 [1]),
    .out_9(\n12或24进制计数器_1_out_9 [0]), .out_10(\n12或24进制计数器_1_out_13 [3]), .out_11(\n12或24进制计数器_1_out_13 [2]),
    .out_12(\n12或24进制计数器_1_out_13 [1]), .out_13(\n12或24进制计数器_1_out_13 [0]));  // open: out_14
  Comparator comparator_1 (
    .a({\n12或24进制计数器_1_out_9 , \n12或24进制计数器_1_out_13 }), .b(8'h11), .gt(comparator_1_gt));  // open: eq, lt
  or or_2 (or_2_out, and_5_out, not_4_out);
  Multiplexer #(.width(8)) multiplexer_3 (
    .in0({\n12或24进制计数器_1_out_9 , \n12或24进制计数器_1_out_13 }), .in1(\n2进制转bcd_1_out_2 ),
    .out({multiplexer_3_out_2, multiplexer_3_out}), .sel(comparator_1_gt));  // open: en
  not not_4 (not_4_out, \n60进制计数器_2_out_13 );
  \_60进制计数器  \u_60进制计数器_1  (
    .CPu(or_2_out), .CPd(and_6_out), .Clr(Clr), .out_13(\n60进制计数器_1_out_13 ), .out_5(out_14[3]),
    .out_6(out_14[2]), .out_7(out_14[1]), .out_8(out_14[0]), .out_9(out_15[3]), .out_10(out_15[2]),
    .out_11(out_15[1]), .out_12(out_15[0]), .Adj(and_4_out));
  \_60进制计数器  \u_60进制计数器_2  (
    .CPu(\n8hz转1hz_1_out_2 ), .CPd(1'b0), .Clr(Clr), .out_13(\n60进制计数器_2_out_13 ), .out_5(out_16[3]),
    .out_6(out_16[2]), .out_7(out_16[1]), .out_8(out_16[0]), .out_9(out_17[3]), .out_10(out_17[2]),
    .out_11(out_17[1]), .out_12(out_17[0]), .Adj(1'b0));
  nor nor_1 (nor_1_out, out_17[0], out_17[1], out_17[2], out_17[3]);
  and and_7 (and_7_out, out_16[0], out_16[2]);
  and and_8 (and_8_out, out_15[0], out_15[3], out_14[0]);
  and and_9 (and_9_out, nor_1_out, and_7_out, and_8_out);
  \整点报时电路  \u_整点报时电路_1  (.in_1(and_9_out), .out_3(out_18), .in_2(in_7));
endmodule

module \数字钟封装  (
  input  in_1,
  input  in_2,
  input  in_3,
  input  in_4
);

  wire button_1_out, button_2_out, clock_1_out, \数字钟电路_1_out_18 ;
  wire [3:0] \数字钟电路_1_out_12 , \数字钟电路_1_out_13 , \数字钟电路_1_out_14 , \数字钟电路_1_out_15 , \数字钟电路_1_out_16 ,
       \数字钟电路_1_out_17 ;
  wire [4:0] \数字钟电路_1_out_8 , \数字钟电路_1_out_9 , \数字钟电路_1_out_10 , \数字钟电路_1_out_11 ;

  DotMatrix #(.matrixcols(4), .matrixrows(5)) dotmatrix_1 (
    .col0(\数字钟电路_1_out_8 ), .col1(\数字钟电路_1_out_9 ), .col2(\数字钟电路_1_out_10 ), .col3(\数字钟电路_1_out_11 ));
  Clock clock_1 (.out(clock_1_out));
  Hex_Digit_Display hex_digit_display_1 (.value(\数字钟电路_1_out_12 ));  // open: dp
  Hex_Digit_Display hex_digit_display_2 (.value(\数字钟电路_1_out_13 ));  // open: dp
  Button button_1 (.out(button_1_out));
  Button button_2 (.out(button_2_out));
  Hex_Digit_Display hex_digit_display_3 (.value(\数字钟电路_1_out_15 ));  // open: dp
  Hex_Digit_Display hex_digit_display_4 (.value(\数字钟电路_1_out_14 ));  // open: dp
  Hex_Digit_Display hex_digit_display_5 (.value(\数字钟电路_1_out_17 ));  // open: dp
  Hex_Digit_Display hex_digit_display_6 (.value(\数字钟电路_1_out_16 ));  // open: dp
  \数字钟电路  \u_数字钟电路_1  (
    .Adj1(in_2), .in_7(clock_1_out), .Adj0(in_1), .CPu(button_2_out), .CPd(button_1_out), .Clr(in_4),
    .out_18(\数字钟电路_1_out_18 ), .in_1(in_3), .out_8(\数字钟电路_1_out_8 ), .out_9(\数字钟电路_1_out_9 ),
    .out_10(\数字钟电路_1_out_10 ), .out_11(\数字钟电路_1_out_11 ), .out_12(\数字钟电路_1_out_12 ),
    .out_13(\数字钟电路_1_out_13 ), .out_14(\数字钟电路_1_out_14 ), .out_15(\数字钟电路_1_out_15 ),
    .out_16(\数字钟电路_1_out_16 ), .out_17(\数字钟电路_1_out_17 ));
  LED led_1 (.in(\数字钟电路_1_out_18 ));
endmodule

module \BCD转2进制  (
  input  [3:0] in_1,
  input  [3:0] in_2,
  output [7:0] out_3
);

  wire [7:0] bit_extender_1_out, bit_extender_2_out;

  assign bit_extender_1_out = {{4{1'b0}}, in_1};  // Bit_Extender bit_extender_1
  assign bit_extender_2_out = {{4{1'b0}}, in_2};  // Bit_Extender bit_extender_2
  Multiplier multiplier_1 (.a(bit_extender_2_out), .b(8'ha), .out(out_3), .cin(bit_extender_1_out));  // open: cout
endmodule

module \_2进制转BCD  (
  input  [7:0] in_1,
  output [7:0] out_2
);

  Divider #(.width(4)) divider_1 (.a(in_1[3:0]), .b(4'b1010), .out(out_2[7:4]), .upper(in_1[7:4]), .rem(out_2[3:0]));
endmodule

module \_8HZ转1HZ封装  (
);

  wire clock_1_out, \n8hz转1hz_1_out_2 ;

  Clock clock_1 (.out(clock_1_out));
  \_8Hz转1Hz  \u_8hz转1hz_1  (.out_2(\n8hz转1hz_1_out_2 ));  // open: in_1
  LED led_1 (.in(\n8hz转1hz_1_out_2 ));
endmodule
