// Logisim project 乘法器.circ as structural Verilog: 4 circuits, main circuit main
module main (
  input  [3:0] a,
  input  [3:0] b,
  input  [3:0] b_2,
  input  [31:0] a_31_0,
  input  [31:0] a_31_0_2,
  input  [31:0] b_3,
  output [7:0] p,
  output [31:0] p_2,
  output [31:0] p_3
);

  wire [31:0] undriven;

  \_4位乘法器  \u_4位乘法器_1  (.b(a), .a(b), .p(p));
  \_32_4乘法器  \u_32_4乘法器_1  (.b_3_0(b_2), .a_31_0(a_31_0), .p_31_0(p_2));
  \_32_32乘法器  \u_32_32乘法器_1  (.a(undriven), .b(b_3), .p(p_3));
endmodule

module \_4位乘法器  (
  input  [3:0] b,
  input  [3:0] a,
  output [7:0] p
);

  wire [7:0] adder_1_out, adder_2_out, adder_3_out, adder_4_out, bit_extender_1_out, multiplexer_1_out,
       multiplexer_2_out, multiplexer_3_out, shifter_1_out, shifter_2_out, shifter_3_out;

  Adder adder_1 (.a({8{1'b0}}), .b(bit_extender_1_out), .out(adder_1_out));  // open: cin, cout
  assign bit_extender_1_out = {{4{1'b0}}, a};  // Bit_Extender bit_extender_1
  Multiplexer #(.width(8), .enable("false")) multiplexer_1 (
    .in0({8{1'b0}}), .in1(adder_1_out), .out(multiplexer_1_out), .sel(b[0]));
  Shifter shifter_1 (.in(bit_extender_1_out), .\dist (3'b001), .out(shifter_1_out));
  Adder adder_2 (.a(multiplexer_1_out), .b(shifter_1_out), .out(adder_2_out));  // open: cin, cout
  Multiplexer #(.width(8), .enable("false")) multiplexer_2 (
    .in0(multiplexer_1_out), .in1(adder_2_out), .out(multiplexer_2_out), .sel(b[1]));
  Shifter shifter_2 (.in(shifter_1_out), .\dist (3'b001), .out(shifter_2_out));
  Adder adder_3 (.a(multiplexer_2_out), .b(shifter_2_out), .out(adder_3_out));  // open: cin, cout
  Multiplexer #(.width(8), .enable("false")) multiplexer_3 (
    .in0(multiplexer_2_out), .in1(adder_3_out), .out(multiplexer_3_out), .sel(b[2]));
  Shifter shifter_3 (.in(shifter_2_out), .\dist (3'b001), .out(shifter_3_out));
  Adder adder_4 (.a(multiplexer_3_out), .b(shifter_3_out), .out(adder_4_out));  // open: cin, cout
  Multiplexer #(.width(8), .enable("false")) multiplexer_4 (
    .in0(multiplexer_3_out), .in1(adder_4_out), .out(p), .sel(b[3]));
endmodule

module \_32_4乘法器  (
  input  [3:0] b_3_0,
  input  [31:0] a_31_0,
  output [31:0] p_31_0
);

  wire [31:0] adder_1_out, adder_2_out, adder_3_out, adder_4_out, multiplexer_1_out, multiplexer_2_out,
       multiplexer_3_out, shifter_1_out, shifter_2_out, shifter_3_out;

  Adder #(.width(32)) adder_1 (.a({32{1'b0}}), .b(a_31_0), .out(adder_1_out));  // open: cin, cout
  Multiplexer #(.width(32), .enable("false")) multiplexer_1 (
    .in0({32{1'b0}}), .in1(adder_1_out), .out(multiplexer_1_out), .sel(b_3_0[0]));
  Shifter #(.width(32)) shifter_1 (.in(a_31_0), .\dist (5'b00001), .out(shifter_1_out));
  Adder #(.width(32)) adder_2 (.a(multiplexer_1_out), .b(shifter_1_out), .out(adder_2_out));  // open: cin, cout
  Multiplexer #(.width(32), .enable("false")) multiplexer_2 (
    .in0(multiplexer_1_out), .in1(adder_2_out), .out(multiplexer_2_out), .sel(b_3_0[1]));
  Shifter #(.width(32)) shifter_2 (.in(shifter_1_out), .\dist (5'b00001), .out(shifter_2_out));
  Adder #(.width(32)) adder_3 (.a(multiplexer_2_out), .b(shifter_2_out), .out(adder_3_out));  // open: cin, cout
  Multiplexer #(.width(32), .enable("false")) multiplexer_3 (
    .in0(multiplexer_2_out), .in1(adder_3_out), .out(multiplexer_3_out), .sel(b_3_0[2]));
  Shifter #(.width(32)) shifter_3 (.in(shifter_2_out), .\dist (5'b00001), .out(shifter_3_out));
  Multiplexer #(.width(32), .enable("false")) multiplexer_4 (
    .in0(multiplexer_3_out), .in1(adder_4_out), .out(p_31_0), .sel(b_3_0[3]));
  Adder #(.width(32)) adder_4 (.a(multiplexer_3_out), .b(shifter_3_out), .out(adder_4_out));  // open: cin, cout
endmodule

module \_32_32乘法器  (
  input  [31:0] a,
  input  [31:0] b,
  output [31:0] p
);

  wire [31:0] _2, _3, _4, _5, _6, _7, \n32_4乘法器_1_p_31_0 , \n32_4乘法器_2_p_31_0 , \n32_4乘法器_3_p_31_0 ,
       \n32_4乘法器_4_p_31_0 , \n32_4乘法器_5_p_31_0 , \n32_4乘法器_6_p_31_0 , \n32_4乘法器_7_p_31_0 ,
       \n32_4乘法器_8_p_31_0 , shifter_1_out, shifter_2_out, shifter_3_out, shifter_4_out, shifter_5_out,
       shifter_6_out, shifter_7_out;

  \_32_4乘法器  \u_32_4乘法器_1  (.b_3_0(b[3:0]), .a_31_0(a), .p_31_0(\n32_4乘法器_1_p_31_0 ));
  \_32_4乘法器  \u_32_4乘法器_2  (.b_3_0(b[7:4]), .a_31_0(a), .p_31_0(\n32_4乘法器_2_p_31_0 ));
  \_32_4乘法器  \u_32_4乘法器_3  (.b_3_0(b[11:8]), .a_31_0(a), .p_31_0(\n32_4乘法器_3_p_31_0 ));
  \_32_4乘法器  \u_32_4乘法器_4  (.b_3_0(b[15:12]), .a_31_0(a), .p_31_0(\n32_4乘法器_4_p_31_0 ));
  \_32_4乘法器  \u_32_4乘法器_5  (.b_3_0(b[19:16]), .a_31_0(a), .p_31_0(\n32_4乘法器_5_p_31_0 ));
  \_32_4乘法器  \u_32_4乘法器_6  (.b_3_0(b[23:20]), .a_31_0(a), .p_31_0(\n32_4乘法器_6_p_31_0 ));
  \_32_4乘法器  \u_32_4乘法器_7  (.b_3_0(b[27:24]), .a_31_0(a), .p_31_0(\n32_4乘法器_7_p_31_0 ));
  \_32_4乘法器  \u_32_4乘法器_8  (.b_3_0(b[31:28]), .a_31_0(a), .p_31_0(\n32_4乘法器_8_p_31_0 ));
  Shifter #(.width(32)) shifter_1 (.in(\n32_4乘法器_2_p_31_0 ), .\dist (5'b00100), .out(shifter_1_out));
  Shifter #(.width(32)) shifter_2 (.in(\n32_4乘法器_3_p_31_0 ), .\dist (5'b01000), .out(shifter_2_out));
  Shifter #(.width(32)) shifter_3 (.in(\n32_4乘法器_4_p_31_0 ), .\dist (5'b01100), .out(shifter_3_out));
  Shifter #(.width(32)) shifter_4 (.in(\n32_4乘法器_5_p_31_0 ), .\dist (5'b10000), .out(shifter_4_out));
  Shifter #(.width(32)) shifter_5 (.in(\n32_4乘法器_6_p_31_0 ), .\dist (5'b10100), .out(shifter_5_out));
  Shifter #(.width(32)) shifter_6 (.in(\n32_4乘法器_7_p_31_0 ), .\dist (5'b11000), .out(shifter_6_out));
  Shifter #(.width(32)) shifter_7 (.in(\n32_4乘法器_8_p_31_0 ), .\dist (5'b11100), .out(shifter_7_out));
  Adder #(.width(32)) adder_1 (.a(\n32_4乘法器_1_p_31_0 ), .b(shifter_1_out), .out(_2));  // open: cin, cout
  Adder #(.width(32)) adder_2 (.a(_2), .b(shifter_2_out), .out(_3));  // open: cin, cout
  Adder #(.width(32)) adder_3 (.a(_3), .b(shifter_3_out), .out(_4));  // open: cin, cout
  Adder #(.width(32)) adder_4 (.a(_4), .b(shifter_4_out), .out(_5));  // open: cin, cout
  Adder #(.width(32)) adder_5 (.a(_5), .b(shifter_5_out), .out(_6));  // open: cin, cout
  Adder #(.width(32)) adder_6 (.a(_6), .b(shifter_6_out), .out(_7));  // open: cin, cout
  Adder #(.width(32)) adder_7 (.a(_7), .b(shifter_7_out), .out(p));  // open: cin, cout
endmodule
