// Logisim project 斐波那契.circ as structural Verilog: 6 circuits, main circuit main
module main (
  input  [5:0] in_1
);

  wire button_1_out, button_2_out, controller_1_out_4, controller_1_out_5, controller_1_out_6,
       controller_1_out_7;
  wire [3:0] dispiay_1_d0, dispiay_1_d1, dispiay_1_d2, dispiay_1_out_5, dispiay_1_out_6, dispiay_1_out_7,
       dispiay_1_out_8, dispiay_1_out_9, dispiay_1_out_10, dispiay_1_out_11;
  wire [31:0] fibo_1_out_5;

  Button button_1 (.out(button_1_out));
  Button button_2 (.out(button_2_out));
  Controller controller_1 (
    .n(in_1), .clear(button_1_out), .clock(button_2_out), .out_4(controller_1_out_4),
    .out_5(controller_1_out_5), .out_6(controller_1_out_6), .out_7(controller_1_out_7));
  Fibo fibo_1 (
    .out_5(fibo_1_out_5), .start(controller_1_out_5), .clr(controller_1_out_7), .clk(controller_1_out_6),
    .n_i_1(controller_1_out_4));
  Dispiay dispiay_1 (
    .in_1(fibo_1_out_5), .D0(dispiay_1_d0), .D1(dispiay_1_d1), .D2(dispiay_1_d2), .out_5(dispiay_1_out_5),
    .out_6(dispiay_1_out_6), .out_7(dispiay_1_out_7), .out_8(dispiay_1_out_8), .out_9(dispiay_1_out_9),
    .out_10(dispiay_1_out_10), .out_11(dispiay_1_out_11));
  Hex_Digit_Display hex_digit_display_1 (.value(dispiay_1_out_11));  // open: dp
  Hex_Digit_Display hex_digit_display_2 (.value(dispiay_1_out_10));  // open: dp
  Hex_Digit_Display hex_digit_display_3 (.value(dispiay_1_out_9));  // open: dp
  Hex_Digit_Display hex_digit_display_4 (.value(dispiay_1_out_7));  // open: dp
  Hex_Digit_Display hex_digit_display_5 (.value(dispiay_1_out_8));  // open: dp
  Hex_Digit_Display hex_digit_display_6 (.value(dispiay_1_out_6));  // open: dp
  Hex_Digit_Display hex_digit_display_7 (.value(dispiay_1_out_5));  // open: dp
  Hex_Digit_Display hex_digit_display_8 (.value(dispiay_1_d1));  // open: dp
  Hex_Digit_Display hex_digit_display_9 (.value(dispiay_1_d2));  // open: dp
  Hex_Digit_Display hex_digit_display_10 (.value(dispiay_1_d0));  // open: dp
endmodule

module sqrX (
  input  [31:0] a,
  input  [31:0] b,
  input  [31:0] c,
  input  [31:0] d,
  output [31:0] out_5,
  output [31:0] out_6,
  output [31:0] out_7,
  output [31:0] out_8
);

  wire [31:0] multiplier_1_out, multiplier_2_out, multiplier_3_out, multiplier_4_out, multiplier_5_out,
       multiplier_6_out, multiplier_7_out;

  Multiplier #(.width(32)) multiplier_1 (.a(a), .b(a), .out(multiplier_1_out));  // open: cin, cout
  Multiplier #(.width(32)) multiplier_2 (.a(a), .b(b), .out(multiplier_2_out));  // open: cin, cout
  Multiplier #(.width(32)) multiplier_3 (.a(a), .b(c), .out(multiplier_3_out));  // open: cin, cout
  Multiplier #(.width(32)) multiplier_4 (.a(b), .b(c), .out(multiplier_4_out));  // open: cin, cout
  Multiplier #(.width(32)) multiplier_5 (.a(b), .b(d), .out(multiplier_5_out));  // open: cin, cout
  Multiplier #(.width(32)) multiplier_6 (.a(c), .b(d), .out(multiplier_6_out));  // open: cin, cout
  Multiplier #(.width(32)) multiplier_7 (.a(d), .b(d), .out(multiplier_7_out));  // open: cin, cout
  Adder #(.width(32)) adder_1 (.a(multiplier_1_out), .b(multiplier_4_out), .out(out_5));  // open: cin, cout
  Adder #(.width(32)) adder_2 (.a(multiplier_2_out), .b(multiplier_5_out), .out(out_6));  // open: cin, cout
  Adder #(.width(32)) adder_3 (.a(multiplier_3_out), .b(multiplier_6_out), .out(out_7));  // open: cin, cout
  Adder #(.width(32)) adder_4 (.a(multiplier_4_out), .b(multiplier_7_out), .out(out_8));  // open: cin, cout
endmodule

module sqrX_A (
  input  [31:0] a,
  input  [31:0] b,
  input  [31:0] c,
  input  [31:0] d,
  output [31:0] out_5,
  output [31:0] out_6,
  output [31:0] out_7,
  output [31:0] out_8
);

  wire [31:0] adder_1_out, adder_5_out, multiplier_1_out, multiplier_2_out, multiplier_3_out,
       multiplier_4_out, multiplier_5_out, multiplier_6_out, multiplier_7_out;

  Multiplier #(.width(32)) multiplier_1 (.a(a), .b(a), .out(multiplier_1_out));  // open: cin, cout
  Multiplier #(.width(32)) multiplier_2 (.a(a), .b(b), .out(multiplier_2_out));  // open: cin, cout
  Multiplier #(.width(32)) multiplier_3 (.a(a), .b(c), .out(multiplier_3_out));  // open: cin, cout
  Multiplier #(.width(32)) multiplier_4 (.a(b), .b(c), .out(multiplier_4_out));  // open: cin, cout
  Multiplier #(.width(32)) multiplier_5 (.a(b), .b(d), .out(multiplier_5_out));  // open: cin, cout
  Multiplier #(.width(32)) multiplier_6 (.a(c), .b(d), .out(multiplier_6_out));  // open: cin, cout
  Multiplier #(.width(32)) multiplier_7 (.a(d), .b(d), .out(multiplier_7_out));  // open: cin, cout
  Adder #(.width(32)) adder_1 (.a(multiplier_1_out), .b(multiplier_4_out), .out(adder_1_out));  // open: cin, cout
  Adder #(.width(32)) adder_2 (.a(adder_1_out), .b(out_6), .out(out_5));  // open: cin, cout
  Adder #(.width(32)) adder_3 (.a(multiplier_2_out), .b(multiplier_5_out), .out(out_6));  // open: cin, cout
  Adder #(.width(32)) adder_4 (.a(multiplier_4_out), .b(multiplier_7_out), .out(out_7));  // open: cin, cout
  Adder #(.width(32)) adder_5 (.a(multiplier_3_out), .b(multiplier_6_out), .out(adder_5_out));  // open: cin, cout
  Adder #(.width(32)) adder_6 (.a(out_7), .b(adder_5_out), .out(out_8));  // open: cin, cout
endmodule

module Fibo (
  input  start,
  input  clr,
  input  clk,
  input  n_i_1,
  output [31:0] out_5
);

  wire and_1_out, multiplexer_5_out, not_1_out;
  wire [31:0] multiplexer_1_out, multiplexer_2_out, multiplexer_3_out, multiplexer_4_out, multiplexer_6_out,
       multiplexer_7_out, multiplexer_8_out, multiplexer_9_out, register_1_q, register_3_q, register_4_q,
       sqrx_1_out_5, sqrx_1_out_6, sqrx_1_out_7, sqrx_1_out_8, sqrx_a_1_out_5, sqrx_a_1_out_6,
       sqrx_a_1_out_7, sqrx_a_1_out_8;

  and and_1 (and_1_out, start, not_1_out);
  not not_1 (not_1_out, clr);
  Multiplexer #(.width(32)) multiplexer_1 (
    .in0({32{1'b0}}), .in1(multiplexer_6_out), .out(multiplexer_1_out), .sel(and_1_out));  // open: en
  Multiplexer #(.width(32)) multiplexer_2 (
    .in0(32'h1), .in1(multiplexer_7_out), .out(multiplexer_2_out), .sel(and_1_out));  // open: en
  Multiplexer #(.width(32)) multiplexer_3 (
    .in0(32'h1), .in1(multiplexer_8_out), .out(multiplexer_3_out), .sel(and_1_out));  // open: en
  Multiplexer #(.width(32)) multiplexer_4 (
    .in0(32'h1), .in1(multiplexer_9_out), .out(multiplexer_4_out), .sel(and_1_out));  // open: en
  Multiplexer multiplexer_5 (.in0(clk), .in1(clr), .out(multiplexer_5_out), .sel(clr));  // open: en
  Register #(.width(32), .trigger("falling")) register_1 (
    .D(multiplexer_1_out), .Q(register_1_q), .clk(multiplexer_5_out));  // open: en, clr
  Register #(.width(32), .trigger("falling")) register_2 (
    .D(multiplexer_2_out), .Q(out_5), .clk(multiplexer_5_out));  // open: en, clr
  Register #(.width(32), .trigger("falling")) register_3 (
    .D(multiplexer_3_out), .Q(register_3_q), .clk(multiplexer_5_out));  // open: en, clr
  Register #(.width(32), .trigger("falling")) register_4 (
    .D(multiplexer_4_out), .Q(register_4_q), .clk(multiplexer_5_out));  // open: en, clr
  sqrX sqrx_1 (
    .a(register_1_q), .b(out_5), .c(register_3_q), .d(register_4_q), .out_5(sqrx_1_out_5),
    .out_6(sqrx_1_out_6), .out_7(sqrx_1_out_7), .out_8(sqrx_1_out_8));
  sqrX_A sqrx_a_1 (
    .a(register_1_q), .b(out_5), .c(register_3_q), .d(register_4_q), .out_6(sqrx_a_1_out_6),
    .out_5(sqrx_a_1_out_5), .out_7(sqrx_a_1_out_7), .out_8(sqrx_a_1_out_8));
  Multiplexer #(.width(32)) multiplexer_6 (
    .in0(sqrx_1_out_5), .in1(sqrx_a_1_out_6), .out(multiplexer_6_out), .sel(n_i_1));  // open: en
  Multiplexer #(.width(32)) multiplexer_7 (
    .in0(sqrx_1_out_6), .in1(sqrx_a_1_out_5), .out(multiplexer_7_out), .sel(n_i_1));  // open: en
  Multiplexer #(.width(32)) multiplexer_8 (
    .in0(sqrx_1_out_7), .in1(sqrx_a_1_out_7), .out(multiplexer_8_out), .sel(n_i_1));  // open: en
  Multiplexer #(.width(32)) multiplexer_9 (
    .in0(sqrx_1_out_8), .in1(sqrx_a_1_out_8), .out(multiplexer_9_out), .sel(n_i_1));  // open: en
endmodule

module Dispiay (
  input  [31:0] in_1,
  output [3:0] D0,
  output [3:0] D1,
  output [3:0] D2,
  output [3:0] out_5,
  output [3:0] out_6,
  output [3:0] out_7,
  output [3:0] out_8,
  output [3:0] out_9,
  output [3:0] out_10,
  output [3:0] out_11
);

  wire [31:0] divider_1_out, divider_2_out, divider_3_out, divider_4_out, divider_5_out, divider_6_out,
       divider_7_out, divider_8_out, divider_9_out;
  wire [31:4] divider_1_rem, divider_2_rem, divider_3_rem, divider_4_rem, divider_5_rem, divider_6_rem,
       divider_7_rem, divider_8_rem, divider_9_rem, divider_10_rem;

  Divider #(.width(32)) divider_1 (
    .a(in_1), .b(32'ha), .out(divider_1_out), .upper({32{1'b0}}), .rem({divider_1_rem, D0}));
  Divider #(.width(32)) divider_2 (
    .a(divider_1_out), .b(32'ha), .out(divider_2_out), .upper({32{1'b0}}), .rem({divider_2_rem, D1}));
  Divider #(.width(32)) divider_3 (
    .a(divider_2_out), .b(32'ha), .out(divider_3_out), .upper({32{1'b0}}), .rem({divider_3_rem, D2}));
  Divider #(.width(32)) divider_4 (
    .a(divider_3_out), .b(32'ha), .out(divider_4_out), .upper({32{1'b0}}), .rem({divider_4_rem, out_5}));
  Divider #(.width(32)) divider_5 (
    .a(divider_4_out), .b(32'ha), .out(divider_5_out), .upper({32{1'b0}}), .rem({divider_5_rem, out_6}));
  Divider #(.width(32)) divider_6 (
    .a(divider_5_out), .b(32'ha), .out(divider_6_out), .upper({32{1'b0}}), .rem({divider_6_rem, out_7}));
  Divider #(.width(32)) divider_7 (
    .a(divider_8_out), .b(32'ha), .out(divider_7_out), .upper({32{1'b0}}), .rem({divider_7_rem, out_9}));
  Divider #(.width(32)) divider_8 (
    .a(divider_6_out), .b(32'ha), .out(divider_8_out), .upper({32{1'b0}}), .rem({divider_8_rem, out_8}));
  Divider #(.width(32)) divider_9 (
    .a(divider_7_out), .b(32'ha), .out(divider_9_out), .upper({32{1'b0}}), .rem({divider_9_rem, out_10}));
  Divider #(.width(32)) divider_10 (
    .a(divider_9_out), .b(32'ha), .upper({32{1'b0}}), .rem({divider_10_rem, out_11}));  // open: out
endmodule

module Controller (
  input  [5:0] n,
  input  clear,
  input  clock,
  output out_4,
  output out_5,
  output out_6,
  output out_7
);

  wire and_1_out, comparator_1_gt, multiplexer_1_out, not_1_out, shift_register_1_out;
  wire [2:0] counter_1_q;

  Counter #(.width(3), .max('h7)) counter_1 (
    .count(not_1_out), .Q(counter_1_q), .clk(clock), .clr(clear));  // open: load, D, carry
  Shift_Register #(.length(7)) shift_register_1 (
    .clk(multiplexer_1_out), .out(shift_register_1_out), .load(clear), .d0(n[0]), .d1(n[1]), .d2(n[2]),
    .d3(n[3]), .d4(n[4]), .d5(n[5]));  // open: shift, in, clr, q0, q1, q2, q3, q4, q5, d6, q6
  Multiplexer multiplexer_1 (.in0(clock), .in1(clear), .out(multiplexer_1_out), .sel(clear));  // open: en
  not not_1 (not_1_out, comparator_1_gt);
  Comparator #(.width(3), .mode("unsigned")) comparator_1 (
    .a(counter_1_q), .b(3'b110), .gt(comparator_1_gt));  // open: eq, lt
  and and_1 (and_1_out, shift_register_1_out, clock);
  and and_2 (out_6, not_1_out, clock);
  D_Flip_Flop #(.trigger("falling")) d_ff_1 (
    .clk(and_1_out), .D(1'b1), .Q(out_5), .reset(clear));  // open: Qn, preset, en
  and and_3 (out_4, shift_register_1_out, out_5);

  assign out_7 = clear;
endmodule
